# Fritzing sketch PiFan (saved by Fritzing 0.9.3b)

parts:
  Raspberry_Pi_1 = Raspberry Pi 3 [part_number=RPI-3-V1.2]
  R1 = Resistor [tolerance=±5% resistance=4.7k package="0402 [SMD]"]
  Q1 = NPN-Transistor [package="TO92 [THT]"]
  F1 = Fan - Ventilador [package=THT]
  D1 = Diode [package=diode-1n4001]

nets:
  N1: Raspberry_Pi_1.GPIO6, R1.Pin_1
  GND: Raspberry_Pi_1.GND, Q1.E, D1.A
  5V: Raspberry_Pi_1.5V, F1.5V
  N2: R1.Pin_0, Q1.B
  N3: Q1.C, F1.GND, D1.C

custom parts:
  Fan - Ventilador: Ventilador de 2 pines, se encuentra comunmente en computadoras de escritorio
